# Fritzing sketch アイケアマネージャー (saved by Fritzing 0.9.3b)
breadboards: 1

parts:
  LED1 = LED - 5mm [color="Red (633nm)" package="5 mm [THT]"]
  LED2 = LED - 5mm [color="Red (633nm)" package="5 mm [THT]"]
  hc-sr1 = hc-sr04
  R1 = Resistor [tolerance=±5% resistance=220 package=THT]
  R2 = Resistor [tolerance=±5% resistance=220 package=THT]
  J1 = Piezo Speaker
  A1 = Arduino UNO R4 WiFi

nets:
  N1: LED1.cathode, R2.Pin_1
  N2: LED1.anode, A1.Pin_39
  N3: LED2.cathode, R1.Pin_1
  N4: LED2.anode, A1.Pin_40
  N5: hc-sr1.VCC, A1.Pin_8, A1.Pin_27
  N6: hc-sr1.Trig, A1.Pin_37
  N7: hc-sr1.Echo, A1.Pin_36
  N8: hc-sr1.GND, R1.Pin_0, R2.Pin_0, J1.pin1, A1.Pin_9, A1.Pin_48
  N9: J1.pin2, A1.Pin_41

custom parts:
  Arduino UNO R4 WiFi: The Arduino UNO R4 WiFi merges the RA4M1 microprocessor from Renesas with the ESP32-S3 from Espressif, creating an all-in-one tool for makers with enhanced processing power and a diverse array of new peripherals.
